# Fritzing sketch Fritzing (saved by Fritzing 0.9.3b)
breadboards: 2

parts:
  LED1 = smd LED [color="Red (633nm)" package="1206 [SMD]"]
  R1 = Resistor [tolerance=±5% resistance=220 package="1206 [SMD]"]
  S1 = Momentary Switch [package=tactile-pth]
  KEYPAD1 = Membrane Matrix Keypad
  M1 = DOIT Esp32 DevKit v1 (30 pins long, 11 pins width) [part_number=ESP32S-PIN30]
  R2 = Resistor [tolerance=±5% resistance=220 package="1206 [SMD]"]
  R3 = Resistor [tolerance=±5% resistance=220 package="1206 [SMD]"]
  R4 = Resistor [tolerance=±5% resistance=220 package="1206 [SMD]"]
  R5 = Resistor [tolerance=±5% resistance=220 package="1206 [SMD]"]
  R6 = Resistor [tolerance=±5% resistance=220 package="1206 [SMD]"]
  J1 = Piezo Speaker
  R7 = Resistor [tolerance=±5% resistance=220 package="1206 [SMD]"]
  R8 = Resistor [tolerance=±5% resistance=220 package="1206 [SMD]"]
  R9 = Resistor [tolerance=±5% resistance=220 package="1206 [SMD]"]
  R10 = Resistor [tolerance=±5% resistance=220 package="1206 [SMD]"]
  R11 = Resistor [tolerance=±5% resistance=220 package="1206 [SMD]"]
  R12 = Resistor [tolerance=±5% resistance=220 package="1206 [SMD]"]
  R13 = Resistor [tolerance=±5% resistance=220 package="1206 [SMD]"]
  LED2 = smd LED [color="Red (633nm)" package="1206 [SMD]"]
  R14 = Resistor [tolerance=±5% resistance=220 package="1206 [SMD]"]

nets:
  N1: LED1.cathode, M1.GND, R5.Pin_1, J1.pin1, R7.Pin_1, R12.Pin_1, LED2.cathode
  N2: LED1.anode, R6.Pin_1
  N3: R1.Pin_0, KEYPAD1.1, M1.VP
  N4: R1.Pin_1, S1.3, M1.3V3, R2.Pin_1, R3.Pin_1, R4.Pin_1, R8.Pin_1, R13.Pin_1
  N5: S1.1, M1.D32
  N6: S1.4, R5.Pin_0
  N7: KEYPAD1.2, M1.VN, R2.Pin_0
  N8: KEYPAD1.3, M1.D34, R3.Pin_0
  N9: KEYPAD1.4, M1.D35, R4.Pin_0
  N10: KEYPAD1.5, M1.D14
  N11: KEYPAD1.6, M1.D12
  N12: KEYPAD1.7, M1.D13
  N13: M1.D4, J1.pin2
  N14: M1.D21, R10.Pin_1
  N15: M1.D22, R9.Pin_1
  N16: M1.D33, R14.Pin_0
  N17: M1.D26, R6.Pin_0
  N18: M1.D27, R11.Pin_1
  N19: LED2.anode, R14.Pin_1

notes:
  Relay status LED
  Reset Button
  Buzzer
  RTC
  SDA
  SCL
  VCC
  GND
  Relay
  VCC
  GND
  IN
  Keypad Back Light LED
  All resistors have same value 1k ohm

custom parts:
  Membrane Matrix Keypad: Membrane Matrix 3x4 Keypad
  DOIT Esp32 DevKit v1 (30 pins long, 11 pins width): The DOIT Esp32 DevKit v1 is one of the development board created by DOIT to evaluate the ESP-WROOM-32 module. It is based on the ESP32 microcontroller that boasts Wifi, Bluetooth, Ethernet and Low Power support all in a single chip. (vanepp) made breadboard work, adjusted pin numbering and labels and reduced size of schematic and cleaned up pcb. This chip is 30pins long (2 x15) and 11 pins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
